# Fritzing sketch RelayBoard (saved by Fritzing 0.9.2b)
breadboards: 1

parts:
  Part1 = Arduino Mega 2560 (Rev3)
  J1 = Power Jack [package=power_jack_pth_lock]
  M1 = DC Motor
  M2 = DC Motor
  S1 = Tilt Switch [package=THT]
  J2 = Power Jack [package=power_jack_pth_lock]
  U1 = TOUCH [package=touch2]
  R1 = Resistor [tolerance=±5% resistance=220 package=THT]
  R2 = Resistor [tolerance=±5% resistance=220 package=THT]
  LED1 = LED - 5mm [color="Orange (620nm)" package="5 mm [THT]"]
  S2 = Tilt Switch [package=THT]
  R3 = Resistor [tolerance=±5% resistance=220 package=THT]
  R4 = Resistor [tolerance=±5% resistance=220 package=THT]
  LED4 = LED - 5mm [color="Red (633nm)" package="5 mm [THT]"]
  LED5 = LED - 5mm [color="Red (633nm)" package="5 mm [THT]"]
  LED6 = LED - 5mm [color="Red (633nm)" package="5 mm [THT]"]
  4_Relay_Module1 = OPENMolo 4 Relay breakout board

nets:
  N1: Part1.D9_PWM, S2.Pin_1
  N2: Part1.D8_PWM, S1.Pin_1
  N3: Part1.5V, 4_Relay_Module1.P_VCC
  N4: Part1.GND, J1.GNDBREAK, S1.Pin_2, LED1.cathode, S2.Pin_2, LED4.cathode, LED5.cathode, LED6.cathode, 4_Relay_Module1.P_GND
  N5: Part1.D2_PWM, R4.Pin_0, 4_Relay_Module1.E1
  N6: Part1.D3_PWM, R3.Pin_0, 4_Relay_Module1.E2
  N7: Part1.D4_PWM, R1.Pin_0
  N8: Part1.D5_PWM, R2.Pin_0
  N9: J1.PWR, 4_Relay_Module1.PW_Rel_3, 4_Relay_Module1.PW_Rel_4
  N10: M1.pin_2, 4_Relay_Module1.NO_Rel_3
  N11: M2.pin_2, 4_Relay_Module1.NO_Rel_4
  N12: J2.GNDBREAK, U1.T1
  N13: J2.PWR, 4_Relay_Module1.PW_Rel_1
  N14: U1.T2, 4_Relay_Module1.NO_Rel_1
  N15: R1.Pin_1, LED5.anode
  N16: R2.Pin_1, LED6.anode
  N17: LED1.anode, R3.Pin_1
  N18: R4.Pin_1, LED4.anode

notes:
  Water Level sensors UP
  Pump OUT
  Plant Tank Pump
  12V Power
  Arduino Power
  Ultrasonic Fogger
  24V Power
  LED Strip
  Relay Sim Led
  Pump IN
  FOG
  LAMP
  Water Level sensors DOWN

custom parts:
  OPENMolo 4 Relay breakout board: Módulo de 8 relés de 10A optoaislados pensado para desarrollos rápidos basadon en microcontroladores o microcomputadoras. Estos módulos son diseñados con especial cuidado tanto en sus capacidades aisladoras para preservar equipos de mayor valor asi como en las fijaciones para evitar problemas a la hora de armar un prototipo o de fijarlo en un tablero definitivo. Una importante característica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
