# Fritzing sketch pump (saved by Fritzing 0.9.2b)
breadboards: 1

parts:
  Q1 = NPN-Transistor [package="TO92 [THT]"]
  R1 = Resistor [tolerance=±5% resistance=560 package=THT]
  M1 = DC Motor
  D1 = Rectifier Diode [part_number=1N4001 package="300 mil [THT]"]
  Part1 = Arduino Mega 2560 (Rev3)

nets:
  N1: Q1.E, M1.pin_2, D1.cathode
  N2: Q1.B, R1.Pin_1
  N3: Q1.C, Part1.GND
  N4: R1.Pin_0, Part1.D9_PWM
  N5: M1.pin_1, D1.anode, Part1.5V

notes:
  First schematics to run the pump with the Arduino.
